# Fritzing sketch tagreader_fork (saved by Fritzing 1.0.5)

parts:
  WeMos_D1_Mini1 = WeMos D1 Mini
  LED1 = smd LED [color="Green (560nm)" package="0603 [SMD]"]
  LED2 = smd LED [color="Red (635nm)" package="0603 [SMD]"]
  Part1 = PN532 Elechouse RFID NFC Module V3
  J1 = Piezo Speaker
  DFPlayer_Mini1 = DFPlayer MINI [package="DIP (Dual Inline) [THT]"]
  SP1 = SPEAKER [package=pcb_mount_speaker]
  R1 = Resistor [tolerance=±5% power=0.25W resistance=470 package=THT]
  R2 = Resistor [tolerance=±5% power=0.25W resistance=470 package=THT]

nets:
  3V3: WeMos_D1_Mini1.3V3, DFPlayer_Mini1.VCC
  5V: WeMos_D1_Mini1.5V, Part1.VCC
  N1: WeMos_D1_Mini1.D1, Part1.SDA
  N2: WeMos_D1_Mini1.D2, Part1.SCL
  N3: WeMos_D1_Mini1.D3, DFPlayer_Mini1.RX
  N4: WeMos_D1_Mini1.D4, DFPlayer_Mini1.TX
  N5: WeMos_D1_Mini1.D5, R1.Pin_1
  N6: WeMos_D1_Mini1.D6, R2.Pin_1
  N7: WeMos_D1_Mini1.D7, J1.pin2
  GND: WeMos_D1_Mini1.G, LED2.cathode, Part1.GND, DFPlayer_Mini1.GND
  N8: LED1.anode, R1.Pin_0
  N9: LED2.anode, R2.Pin_0
  N10: DFPlayer_Mini1.SPK1, SP1.-
  N11: DFPlayer_Mini1.SPK2, SP1.+

custom parts:
  PN532 Elechouse RFID NFC Module V3: NFC is a popular technology in recent years. We often heard this work while smart phone company such as Samsung or HTC introduces their latest high-end phones. Almost all the high-end phone in the market support NFC. Near field communication (NFC) is a set of standards for smart phones and similar devices to establish radio communication with each other by touching them together or bringing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
  DFPlayer MINI: MP3 module by DFRobot.com for playing Music from an SD-Card. Supports WAV and MP3 files.
